// Logisim project Cache.circ as structural Verilog
module main (
  input  EnableTestHalting,
  output [9:0] CorrectCounter,
  output [9:0] HitCounter,
  output [9:0] MissCounter,
  output [9:0] TestNumber,
  output [7:0] ByteRead,
  output [7:0] CorrectByteRead,
  output Halt
);

  wire and_3_out, and_4_out, and_5_out, CLK, CmdIsRead, Correct, CpuRead, CpuWrite, DidContain, HaltTesting,
       MaxItersReached, MemRead, MemWrite, not_1_out, not_2_out, not_4_out, NotDoneTesting, Ok2Count,
       or_1_out, Ready;
  wire [7:0] CpuWriteValue, MemAddress;
  wire [9:0] CpuAddress;
  wire [31:0] Line2Mem, LineFromMem;

  not not_1 (not_1_out, Ready);
  Clock clock_1 (.out(CLK));
  or or_1 (or_1_out, MaxItersReached, Ready);
  Counter #(.width(4), .max('h9)) MaxClocks (
    .load(Ready), .D(4'b0001), .count(not_1_out), .carry(MaxItersReached), .clk(CLK));  // open: Q, clr
  and and_1 (HaltTesting, EnableTestHalting, CmdIsRead, not_2_out);
  not not_2 (not_2_out, Correct);
  not not_3 (NotDoneTesting, Halt);
  Inputs inputs_1 (
    .HaltTesting(HaltTesting), .Ready(or_1_out), .CLK(CLK), .Done(Halt), .Read(CpuRead), .Write(CpuWrite),
    .Address(CpuAddress), .Value(CpuWriteValue), .TestNumber(TestNumber));
  Cache cache_1 (
    .CpuAddress(CpuAddress), .CpuRead(CpuRead), .CpuWrite(CpuWrite), .CpuWriteValue(CpuWriteValue),
    .CLK(CLK), .Ready(Ready), .DidContain(DidContain), .ByteRead(ByteRead), .MemAddress(MemAddress),
    .MemRead(MemRead), .MemWrite(MemWrite), .LineFromMem(LineFromMem), .Line2Mem(Line2Mem));
  // Probe on CpuRead
  // Probe on CpuWrite
  // Probe on CpuAddress
  // Probe on CpuWriteValue
  // Probe on TestNumber
  // Probe on CorrectByteRead
  // Probe on Correct
  // Probe on Ready
  // Probe on DidContain
  // Probe on ByteRead
  // Probe on MemAddress
  // Probe on MemRead
  // Probe on MemWrite
  // Probe on HitCounter
  // Probe on LineFromMem
  // Probe on Line2Mem
  not not_4 (not_4_out, HaltTesting);
  RAM #(.dataWidth(32), .bus("separate")) ram_1 (
    .addr(MemAddress), .din(Line2Mem), .data(LineFromMem), .str(MemWrite), .clk(CLK), .ld(MemRead));  // open: sel, clr
  and and_2 (Ok2Count, Ready, not_4_out, NotDoneTesting);
  // Probe on LineFromMem
  and and_3 (and_3_out, Correct, Ok2Count);
  and and_4 (and_4_out, DidContain, Ok2Count);
  and and_5 (and_5_out, MemRead, NotDoneTesting);
  Checker checker_1 (
    .TestNumber(TestNumber), .YourByteRead(ByteRead), .CmdIsRead(CmdIsRead),
    .CorrectByteRead(CorrectByteRead), .Correct(Correct));
  Counter #(.width(10), .max('h3ff)) u_CorrectCounter (
    .count(and_3_out), .Q(CorrectCounter), .clk(CLK));  // open: load, D, carry, clr
  Counter #(.width(10), .max('h3ff)) u_HitCounter (
    .count(and_4_out), .Q(HitCounter), .clk(CLK));  // open: load, D, carry, clr
  Counter #(.width(10), .max('h3ff)) u_MissCounter (
    .count(and_5_out), .Q(MissCounter), .clk(CLK));  // open: load, D, carry, clr
  // Probe on CorrectCounter
  // Probe on HitCounter
  // Probe on MissCounter

  // Other names for the same wires on the sheet: DoneTesting = Halt

  // Notes on the sheet:
  //   Your Answer Inside Here
  //   Aarsh Vyas 999711439
  //   Peregrine Rolland 913626157
endmodule

module Cache (
  input  [9:0] CpuAddress,
  input  CpuRead,
  input  CpuWrite,
  input  [7:0] CpuWriteValue,
  input  CLK,
  input  [31:0] LineFromMem,
  output Ready,
  output DidContain,
  output [7:0] ByteRead,
  output [7:0] MemAddress,
  output MemRead,
  output MemWrite,
  output [31:0] Line2Mem
);

  wire comparator_1_eq, comparator_2_eq, comparator_3_eq, comparator_4_eq, comparator_5_eq, comparator_6_eq,
       DidContain_t, DirtySet, init, MemWrite0, MemWrite1, multiplexer_5_out, Read, Set0Contains, Set0Dirty,
       Set1Contains, Set1Dirty, Start, Write, WriteActual0, WriteActual1;
  wire [1:0] BlockNum;
  wire [2:0] CurState, NextState;
  wire [6:0] multiplexer_9_out, Set0MemAdd, Set1MemAdd, Tag;
  wire [7:0] Set0Value, Set1Value, WriteValue;
  wire [31:0] Set0L2M, Set1L2M;

  or or_1 (Start, CpuRead, CpuWrite);
  D_Flip_Flop d_ff_1 (.clk(CLK), .D(NextState[2]), .Q(CurState[2]));  // open: Qn, preset, en, reset
  D_Flip_Flop d_ff_2 (.clk(CLK), .D(NextState[1]), .Q(CurState[1]));  // open: Qn, preset, en, reset
  D_Flip_Flop d_ff_3 (.clk(CLK), .D(NextState[0]), .Q(CurState[0]));  // open: Qn, preset, en, reset
  FSM fsm_1 (
    .State2(CurState[2]), .State1(CurState[1]), .State0(CurState[0]), .Write(Write), .Dirty(DirtySet),
    .Contains(DidContain_t), .Start(Start), .NextState2(NextState[2]), .NextState1(NextState[1]),
    .NextState0(NextState[0]));
  Register #(.width(10)) State (
    .D(CpuAddress), .en(Ready), .Q({Tag, MemAddress[0], BlockNum}), .clk(CLK));  // open: clr
  Register State_2 (.D(CpuWriteValue), .en(Ready), .Q(WriteValue), .clk(CLK));  // open: clr
  Comparator #(.width(3), .mode("unsigned")) comparator_1 (
    .a(CurState), .b(3'b000), .eq(comparator_1_eq));  // open: gt, lt
  Comparator #(.width(3), .mode("unsigned")) comparator_2 (
    .a(CurState), .b(3'b001), .eq(comparator_2_eq));  // open: gt, lt
  Comparator #(.width(3), .mode("unsigned")) comparator_3 (
    .a(CurState), .b(3'b101), .eq(comparator_3_eq));  // open: gt, lt
  Comparator #(.width(3), .mode("unsigned")) comparator_4 (
    .a(CurState), .b(3'b100), .eq(comparator_4_eq));  // open: gt, lt
  Comparator #(.width(3), .mode("unsigned")) comparator_5 (
    .a(CurState), .b(3'b111), .eq(comparator_5_eq));  // open: gt, lt
  Register #(.width(1)) State_3 (.D(CpuRead), .en(Ready), .Q(Read), .clk(CLK));  // open: clr
  Register #(.width(1)) State_4 (.D(CpuWrite), .en(Ready), .Q(Write), .clk(CLK));  // open: clr
  Multiplexer #(.enable("false")) multiplexer_1 (.in0(1'b0), .in1(1'b1), .out(init), .sel(comparator_1_eq));
  Multiplexer #(.enable("false")) multiplexer_2 (.in0(1'b0), .in1(1'b1), .out(Ready), .sel(comparator_2_eq));
  Multiplexer #(.enable("false")) multiplexer_3 (.in0(1'b0), .in1(1'b1), .out(MemWrite), .sel(comparator_3_eq));
  Demultiplexer #(.enable("false")) demultiplexer_1 (
    .out0(MemWrite0), .out1(MemWrite1), .in(MemRead), .sel(MemAddress[0]));
  Multiplexer #(.enable("false")) multiplexer_4 (.in0(1'b0), .in1(1'b1), .out(MemRead), .sel(comparator_4_eq));
  Multiplexer #(.enable("false")) multiplexer_5 (
    .in0(1'b0), .in1(1'b1), .out(multiplexer_5_out), .sel(comparator_5_eq));
  Demultiplexer #(.enable("false")) demultiplexer_2 (
    .out0(WriteActual0), .out1(WriteActual1), .in(multiplexer_5_out), .sel(MemAddress[0]));
  Set Set0 (
    .Tag(Tag), .Offset(BlockNum), .init(init), .Write(WriteActual0), .WriteValue(WriteValue),
    .MemWrite(MemWrite0), .LineFromMem(LineFromMem), .CLK(CLK), .Contains(Set0Contains), .IsDirty(Set0Dirty),
    .ByteRead(Set0Value), .Tag2Mem(Set0MemAdd), .Line2Mem(Set0L2M));
  Set Set1 (
    .Tag(Tag), .Offset(BlockNum), .init(init), .Write(WriteActual1), .WriteValue(WriteValue),
    .MemWrite(MemWrite1), .LineFromMem(LineFromMem), .CLK(CLK), .Contains(Set1Contains), .IsDirty(Set1Dirty),
    .ByteRead(Set1Value), .Tag2Mem(Set1MemAdd), .Line2Mem(Set1L2M));
  Register #(.width(1)) State_5 (.D(DidContain_t), .en(comparator_6_eq), .Q(DidContain), .clk(CLK));  // open: clr
  Comparator #(.width(3), .mode("unsigned")) comparator_6 (
    .a(CurState), .b(3'b010), .eq(comparator_6_eq));  // open: gt, lt
  Multiplexer #(.enable("false")) multiplexer_6 (
    .in0(Set0Contains), .in1(Set1Contains), .out(DidContain_t), .sel(MemAddress[0]));
  Multiplexer #(.enable("false")) multiplexer_7 (.in0(Set0Dirty), .in1(Set1Dirty), .out(DirtySet), .sel(MemAddress[0]));
  // Probe on Set0Value
  // Probe on Set1Value
  Multiplexer #(.width(8), .enable("false")) multiplexer_8 (
    .in0(Set0Value), .in1(Set1Value), .out(ByteRead), .sel(MemAddress[0]));
  Multiplexer #(.width(7), .enable("false")) multiplexer_9 (
    .in0(Set0MemAdd), .in1(Set1MemAdd), .out(multiplexer_9_out), .sel(MemAddress[0]));
  Multiplexer #(.width(32), .enable("false")) multiplexer_10 (
    .in0(Set0L2M), .in1(Set1L2M), .out(Line2Mem), .sel(MemAddress[0]));
  Multiplexer #(.width(7), .enable("false")) multiplexer_11 (
    .in0(multiplexer_9_out), .in1(Tag), .out(MemAddress[7:1]), .sel(MemRead));

  // Other names for the same wires on the sheet: WorkingAddress[9:0] = {Tag, MemAddress[0], BlockNum};
  //   DidContainFinal = DidContain; SetNum = MemAddress[0]; WorkingLine[7:0] = {Tag, MemAddress[0]};
  //   MemAddress_t[6:0] = MemAddress[7:1]; SetValueFinal[7:0] = ByteRead

  // Notes on the sheet:
  //   Address Bits = 10
  //   Line Size = 4
  //   W = 3
  //   Num Sets = 2
  //   FSM
  //   C =4*3*2 = 24bytes
  //   Tag bits = 7
  //   Control Signals
  //   The Sets
  //   State Dependant Outputs
  //   Choosing outputs from sets
endmodule

module Inputs (
  input  HaltTesting,
  input  Ready,
  input  CLK,
  output Done,
  output Read,
  output Write,
  output [9:0] Address,
  output [7:0] Value,
  output [9:0] TestNumber
);

  wire and_1_out, not_1_out, not_2_out;

  not not_1 (not_1_out, HaltTesting);
  not not_2 (not_2_out, Done);
  Counter #(.width(10), .max('h3ff), .ongoal("stay")) u_TestNumber (
    .count(and_1_out), .Q(TestNumber), .clk(CLK));  // open: load, D, carry, clr
  and and_1 (and_1_out, not_1_out, Ready, not_2_out);
  ROM #(.addrWidth(10), .dataWidth(21)) rom_1 (
    .addr(TestNumber), .data({Done, Read, Write, Address, Value}));  // open: sel

  // Notes on the sheet:
  //   contents of rom_1 (hex, n*v repeats v):
  //   80882 83fe6 4306b 83e0e 43701 42275 8280f 80304 41bd8 84371 43f77 41d70 4250b 44733 8253d 440d8
  //   82691 440c9 83d7c 43558 446bf 83837 842c9 43e0f 4059d 41556 80166 833b0 43a89 83142 8361c 42e66
  //   43eb6 42c00 43a0e 8165c 84682 8092a 83907 41f89 817b0 40855 82056 425e8 43ff2 8039f 42bd7 82137
  //   4416b 40273 8324a 814e4 44570 41c0f 429da 82640 8069c 8099e 414d5 41004 81beb 84113 419b1 81add
  //   83f35 425ff 829cd 40250 82945 4366d 40cc2 444f8 80814 81156 8446d 42a82 42bae 82578 41135 405d0
  //   8304b 82b3a 40972 822ba 4443a 42337 82506 80bd3 80560 83552 83955 81434 43096 43da1 81aa2 80305
  //   428e6 428cc 808a2 40e80 845f0 4215d 82765 82e29 40be5 82b74 42715 417a2 41fab 8452f 81c0a 83325
  //   44624 80205 42dfc 41333 40958 81348 42736 41069 84510 44669 826dd 8067e 408e4 44680 444e8 832ad
  //   821f8 83509 82d46 81184 432cd 80b77 4005a 440e0 81ea0 43d73 42b8c 80624 41468 42699 415ed 80fc1 0
  //   100000
endmodule

module Checker (
  input  [9:0] TestNumber,
  input  [7:0] YourByteRead,
  output CmdIsRead,
  output [7:0] CorrectByteRead,
  output Correct
);

  wire comparator_1_eq;
  wire [9:0] subtractor_1_out;

  // Probe on TestNumber
  Subtractor #(.width(10)) subtractor_1 (.a(TestNumber), .b(10'h1), .out(subtractor_1_out));  // open: bin, bout
  ROM #(.addrWidth(10), .dataWidth(9)) rom_1 (
    .addr(subtractor_1_out), .data({CmdIsRead, CorrectByteRead}));  // open: sel
  Comparator #(.mode("unsigned")) comparator_1 (
    .a(YourByteRead), .b(CorrectByteRead), .eq(comparator_1_eq));  // open: gt, lt
  and and_1 (Correct, comparator_1_eq, CmdIsRead);

  // Other names for the same wires on the sheet: Test_Number[9:0] = TestNumber

  // Notes on the sheet:
  //   Read Solutions
  //   contents of rom_1 (hex, n*v repeats v):
  //   1a3 1dc 6b 125 1 75 1dc 1c3 d8 1ab 77 70 b 33 10b d8 1c3 c9 174 58 bf 153 199 f 9d 56 1bb 13b 89 16c
  //   180 66 b6 0 e 107 1bf 1d8 167 89 118 55 1a2 e8 f2 1c3 d7 142 6b 73 1ab 18c 70 f da 1c3 14c 1d8 d5 4
  //   1d8 16b b1 1f4 1f2 ff 1da 50 1da 6d c2 f8 155 1c6 1f8 82 ae 1ff 35 d0 16b 1ae 72 175 3a 37 1ff 173
  //   1d0 158 167 1d5 96 a1 1f4 1c3 e6 cc 155 80 170 5d 1e6 166 e5 1ae 15 a2 ab 170 10f 13b 24 150 fc 33
  //   58 133 36 69 170 69 1c3 14c e4 80 e8 1ab 15d 158 1fc 135 cd 1e5 5a e0 104 73 8c 14c 68 99 ed 1a6
endmodule

module Set (
  input  [6:0] Tag,
  input  [1:0] Offset,
  input  init,
  input  Write,
  input  [7:0] WriteValue,
  input  MemWrite,
  input  [31:0] LineFromMem,
  input  CLK,
  output Contains,
  output IsDirty,
  output [7:0] ByteRead,
  output [6:0] Tag2Mem,
  output [31:0] Line2Mem
);

  wire BlockWrite0, BlockWrite1, BlockWrite2, C0, C1, C2, comparator_1_eq, comparator_2_eq, comparator_3_eq,
       comparator_4_gt, comparator_5_gt, comparator_6_gt, comparator_7_eq, comparator_8_eq, comparator_9_gt,
       comparator_10_eq, D0, D1, D2, UpdateAge, Write0, Write1, Write2;
  wire [1:0] adder_1_out, adder_2_out, adder_3_out, Age0, Age1, Age2, ChosenAge, ChosenBlock, EvictedBlock,
       InputAge0, InputAge1, InputAge2, multiplexer_7_out, multiplexer_8_out, multiplexer_9_out,
       multiplexer_12_out, multiplexer_13_out, multiplexer_14_out, multiplexer_15_out, multiplexer_16_out,
       multiplexer_17_out, multiplexer_18_out, multiplexer_22_out, NewAge0, NewAge1, NewAge2, register_1_q,
       register_2_q, register_3_q, register_4_q, register_5_q, register_6_q, State_2_q, State_3_q;
  wire [6:0] Tag0Mem, Tag1Mem, Tag2Mem_t;
  wire [7:0] ChosenValue, multiplexer_1_out, multiplexer_5_out, State_q, Value0, Value1, Value2;
  wire [31:0] L2M0, L2M1, L2M2;

  Block Block0 (
    .LineFromMem(LineFromMem), .Age(InputAge0), .Tag(Tag), .WriteVal(WriteValue), .Offset(Offset),
    .init(init), .UpdateAge(UpdateAge), .Write(Write0), .Evict(BlockWrite0), .CLK(CLK), .Tag2Mem(Tag0Mem),
    .Line2Mem(L2M0), .ReadValue(Value0), .Contained(C0), .Dirty(D0), .Age_2(Age0));
  Register State (.D(ByteRead), .Q(State_q), .clk(CLK), .clr(init));  // open: en
  or or_1 (Contains, C0, C1, C2);
  Register #(.width(2)) register_1 (.D(Age0), .Q(register_1_q), .clk(CLK));  // open: en, clr
  Register #(.width(2)) register_2 (.D(Age1), .Q(register_2_q), .clk(CLK));  // open: en, clr
  Register #(.width(2)) register_3 (.D(Age2), .Q(register_3_q), .clk(CLK));  // open: en, clr
  // Probe on Age0
  Multiplexer #(.width(8), .enable("false")) multiplexer_1 (
    .in0(State_q), .in1(Value0), .out(multiplexer_1_out), .sel(C0));
  Multiplexer #(.width(2), .enable("false")) multiplexer_2 (
    .in0(register_1_q), .in1(NewAge0), .out(InputAge0), .sel(UpdateAge));
  Multiplexer #(.width(2), .enable("false")) multiplexer_3 (
    .in0(register_2_q), .in1(NewAge1), .out(InputAge1), .sel(UpdateAge));
  Multiplexer #(.width(2), .enable("false")) multiplexer_4 (
    .in0(register_3_q), .in1(NewAge2), .out(InputAge2), .sel(UpdateAge));
  Multiplexer #(.width(8), .enable("false")) multiplexer_5 (
    .in0(multiplexer_1_out), .in1(Value1), .out(multiplexer_5_out), .sel(C1));
  // Probe on ChosenBlock
  // Probe on InputAge0
  // Probe on InputAge1
  // Probe on InputAge2
  // Probe on ChosenBlock
  Register #(.width(2)) State_2 (.D(ChosenBlock), .Q(State_2_q), .clk(CLK));  // open: en, clr
  Demultiplexer #(.select(2), .enable("false")) demultiplexer_1 (
    .out0(Write0), .out1(Write1), .out2(Write2), .in(Write), .sel(ChosenBlock));  // open: out3
  Block Block1 (
    .LineFromMem(LineFromMem), .Age(InputAge1), .Tag(Tag), .WriteVal(WriteValue), .Offset(Offset),
    .init(init), .UpdateAge(UpdateAge), .Write(Write1), .Evict(BlockWrite1), .CLK(CLK), .Tag2Mem(Tag1Mem),
    .Line2Mem(L2M1), .ReadValue(Value1), .Contained(C1), .Dirty(D1), .Age_2(Age1));
  Multiplexer #(.width(8), .enable("false")) multiplexer_6 (
    .in0(multiplexer_5_out), .in1(Value2), .out(ByteRead), .sel(C2));
  Multiplexer #(.width(2), .enable("false")) multiplexer_7 (
    .in0(State_2_q), .in1(2'b00), .out(multiplexer_7_out), .sel(C0));
  Register #(.width(2)) register_4 (.D(NewAge0), .Q(register_4_q), .clk(CLK));  // open: en, clr
  Register #(.width(2)) register_5 (.D(NewAge1), .Q(register_5_q), .clk(CLK));  // open: en, clr
  Register #(.width(2)) register_6 (.D(NewAge2), .Q(register_6_q), .clk(CLK));  // open: en, clr
  Multiplexer #(.width(2), .enable("false")) multiplexer_8 (
    .in0(multiplexer_7_out), .in1(2'b01), .out(multiplexer_8_out), .sel(C1));
  // Probe on EvictedBlock
  // Probe on ChosenAge
  // Probe on register_6_q
  Multiplexer #(.width(2), .enable("false")) multiplexer_9 (
    .in0(multiplexer_8_out), .in1(2'b10), .out(multiplexer_9_out), .sel(C2));
  Multiplexer #(.width(2), .enable("false")) multiplexer_10 (
    .in0(multiplexer_9_out), .in1(EvictedBlock), .out(ChosenBlock), .sel(MemWrite));
  Comparator #(.width(2), .mode("unsigned")) comparator_1 (
    .a(ChosenAge), .b(Age0), .eq(comparator_1_eq));  // open: gt, lt
  Comparator #(.width(2), .mode("unsigned")) comparator_2 (
    .a(ChosenAge), .b(Age1), .eq(comparator_2_eq));  // open: gt, lt
  Comparator #(.width(2), .mode("unsigned")) comparator_3 (
    .a(ChosenAge), .b(Age2), .eq(comparator_3_eq));  // open: gt, lt
  Demultiplexer #(.select(2), .enable("false")) demultiplexer_2 (
    .out0(BlockWrite0), .out1(BlockWrite1), .out2(BlockWrite2), .in(MemWrite), .sel(ChosenBlock));  // open: out3
  // Probe on ChosenBlock
  // Probe on ChosenBlock
  Multiplexer #(.select(2), .width(2), .enable("false")) multiplexer_11 (
    .in0(Age0), .in1(Age1), .in2(Age2), .in3(2'b00), .out(ChosenAge), .sel(ChosenBlock));
  // Probe on ChosenAge
  Multiplexer #(.width(2), .enable("false")) multiplexer_12 (
    .in0(register_4_q), .in1(2'b00), .out(multiplexer_12_out), .sel(comparator_1_eq));
  Multiplexer #(.width(2), .enable("false")) multiplexer_13 (
    .in0(register_5_q), .in1(2'b00), .out(multiplexer_13_out), .sel(comparator_2_eq));
  Multiplexer #(.width(2), .enable("false")) multiplexer_14 (
    .in0(register_6_q), .in1(2'b00), .out(multiplexer_14_out), .sel(comparator_3_eq));
  Comparator #(.width(2), .mode("unsigned")) comparator_4 (
    .a(ChosenAge), .b(Age0), .gt(comparator_4_gt));  // open: eq, lt
  Adder #(.width(2)) adder_1 (.a(Age0), .b(2'b01), .out(adder_1_out));  // open: cin, cout
  Adder #(.width(2)) adder_2 (.a(Age1), .b(2'b01), .out(adder_2_out));  // open: cin, cout
  Adder #(.width(2)) adder_3 (.a(Age2), .b(2'b01), .out(adder_3_out));  // open: cin, cout
  Block Block2 (
    .LineFromMem(LineFromMem), .Age(InputAge2), .Tag(Tag), .WriteVal(WriteValue), .Offset(Offset),
    .init(init), .UpdateAge(UpdateAge), .Write(Write2), .Evict(BlockWrite2), .CLK(CLK), .Tag2Mem(Tag2Mem_t),
    .Line2Mem(L2M2), .ReadValue(Value2), .Contained(C2), .Dirty(D2), .Age_2(Age2));
  Register #(.width(2)) State_3 (.D(EvictedBlock), .Q(State_3_q), .clk(CLK));  // open: en, clr
  // Probe on EvictedBlock
  Multiplexer #(.width(2), .enable("false")) multiplexer_15 (
    .in0(multiplexer_12_out), .in1(adder_1_out), .out(multiplexer_15_out), .sel(comparator_4_gt));
  Comparator #(.width(2), .mode("unsigned")) comparator_5 (
    .a(ChosenAge), .b(Age1), .gt(comparator_5_gt));  // open: eq, lt
  Multiplexer #(.width(2), .enable("false")) multiplexer_16 (
    .in0(multiplexer_13_out), .in1(adder_2_out), .out(multiplexer_16_out), .sel(comparator_5_gt));
  Comparator #(.width(2), .mode("unsigned")) comparator_6 (
    .a(ChosenAge), .b(Age2), .gt(comparator_6_gt));  // open: eq, lt
  Multiplexer #(.width(2), .enable("false")) multiplexer_17 (
    .in0(multiplexer_14_out), .in1(adder_3_out), .out(multiplexer_17_out), .sel(comparator_6_gt));
  Comparator #(.width(2), .mode("unsigned")) comparator_7 (.a(Age0), .b(2'b10), .eq(comparator_7_eq));  // open: gt, lt
  Multiplexer #(.width(2), .enable("false")) multiplexer_18 (
    .in0(State_3_q), .in1(2'b00), .out(multiplexer_18_out), .sel(comparator_7_eq));
  Multiplexer #(.width(2), .enable("false")) multiplexer_19 (
    .in0(multiplexer_15_out), .in1(2'b00), .out(NewAge0), .sel(init));
  // Probe on NewAge0
  Multiplexer #(.width(2), .enable("false")) multiplexer_20 (
    .in0(multiplexer_16_out), .in1(2'b01), .out(NewAge1), .sel(init));
  // Probe on NewAge1
  Multiplexer #(.width(2), .enable("false")) multiplexer_21 (
    .in0(multiplexer_17_out), .in1(2'b10), .out(NewAge2), .sel(init));
  // Probe on NewAge2
  Comparator #(.width(2), .mode("unsigned")) comparator_8 (.a(Age1), .b(2'b10), .eq(comparator_8_eq));  // open: gt, lt
  Multiplexer #(.width(2), .enable("false")) multiplexer_22 (
    .in0(multiplexer_18_out), .in1(2'b01), .out(multiplexer_22_out), .sel(comparator_8_eq));
  Comparator #(.width(2), .mode("unsigned")) comparator_9 (
    .a(ChosenAge), .b(2'b00), .gt(comparator_9_gt));  // open: eq, lt
  or or_2 (UpdateAge, init, comparator_9_gt);
  // Probe on EvictedBlock
  Comparator #(.width(2), .mode("unsigned")) comparator_10 (
    .a(Age2), .b(2'b10), .eq(comparator_10_eq));  // open: gt, lt
  Multiplexer #(.width(2), .enable("false")) multiplexer_23 (
    .in0(multiplexer_22_out), .in1(2'b10), .out(EvictedBlock), .sel(comparator_10_eq));
  Multiplexer #(.select(2), .width(32), .enable("false")) multiplexer_24 (
    .in0(L2M0), .in1(L2M1), .in2(L2M2), .in3({32{1'b0}}), .out(Line2Mem), .sel(ChosenBlock));
  // Probe on Line2Mem
  // Probe on ChosenBlock
  Multiplexer #(.select(2), .enable("false")) multiplexer_25 (
    .in0(D0), .in1(D1), .in2(D2), .in3(1'b0), .out(IsDirty), .sel(ChosenBlock));
  // Probe on IsDirty
  Multiplexer #(.select(2), .width(7), .enable("false")) multiplexer_26 (
    .in0(Tag0Mem), .in1(Tag1Mem), .in2(Tag2Mem_t), .in3({7{1'b0}}), .out(Tag2Mem), .sel(ChosenBlock));
  // Probe on Tag2Mem
  Multiplexer #(.select(2), .width(8), .enable("false")) multiplexer_27 (
    .in0(Value0), .in1(Value1), .in2(Value2), .in3({8{1'b0}}), .out(ChosenValue), .sel(ChosenBlock));
  // Probe on ChosenValue

  // Other names for the same wires on the sheet: Dirty = IsDirty; Tag2MemFinal[6:0] = Tag2Mem

  // Notes on the sheet:
  //   Choosing Block for age update!
  //   Choosing which block would be evicted if we choose to evict
endmodule

module Block (
  input  [31:0] LineFromMem,
  input  [1:0] Age,
  input  [6:0] Tag,
  input  [7:0] WriteVal,
  input  [1:0] Offset,
  input  init,
  input  UpdateAge,
  input  Write,
  input  Evict,
  input  CLK,
  output [6:0] Tag2Mem,
  output [31:0] Line2Mem,
  output [7:0] ReadValue,
  output Contained,
  output Dirty,
  output [1:0] Age_2
);

  wire comparator_1_eq, comparator_2_eq, comparator_3_eq, comparator_4_eq, comparator_5_eq, comparator_6_eq,
       comparator_7_eq, comparator_8_eq, comparator_9_eq, multiplexer_14_out, multiplexer_15_out, or_1_out,
       or_2_out, Valid;
  wire [1:0] multiplexer_4_out;
  wire [6:0] multiplexer_2_out;
  wire [7:0] multiplexer_1_out, multiplexer_5_out, multiplexer_6_out, multiplexer_7_out, multiplexer_8_out,
       multiplexer_9_out, multiplexer_10_out, multiplexer_11_out, multiplexer_12_out, multiplexer_13_out;
  wire [31:0] multiplexer_16_out, multiplexer_17_out;

  // Probe on Line2Mem
  // Probe on ReadValue
  // Probe on WriteVal
  // Probe on LineFromMem
  Multiplexer #(.width(8), .enable("false")) multiplexer_1 (
    .in0(ReadValue), .in1(WriteVal), .out(multiplexer_1_out), .sel(Write));
  or or_1 (or_1_out, init, UpdateAge);
  Multiplexer #(.width(7), .enable("false")) multiplexer_2 (
    .in0(Tag2Mem), .in1(Tag), .out(multiplexer_2_out), .sel(Evict));
  Register #(.width(7)) BlockTag (.D(multiplexer_2_out), .Q(Tag2Mem), .clk(CLK));  // open: en, clr
  // Probe on Offset
  Multiplexer #(.select(2), .width(8), .enable("false")) multiplexer_3 (
    .in0(Line2Mem[7:0]), .in1(Line2Mem[15:8]), .in2(Line2Mem[23:16]), .in3(Line2Mem[31:24]), .out(ReadValue),
    .sel(Offset));
  // Probe on ReadValue
  Register #(.width(2)) BlockTag_2 (.D(multiplexer_4_out), .Q(Age_2), .clk(CLK));  // open: en, clr
  Multiplexer #(.width(2), .enable("false")) multiplexer_4 (
    .in0(Age_2), .in1(Age), .out(multiplexer_4_out), .sel(or_1_out));
  Comparator #(.width(2), .mode("unsigned")) comparator_1 (
    .a(Offset), .b(2'b00), .eq(comparator_1_eq));  // open: gt, lt
  Multiplexer #(.width(8), .enable("false")) multiplexer_5 (
    .in0(Line2Mem[7:0]), .in1(multiplexer_1_out), .out(multiplexer_5_out), .sel(comparator_1_eq));
  Comparator #(.width(2), .mode("unsigned")) comparator_2 (
    .a(Offset), .b(2'b01), .eq(comparator_2_eq));  // open: gt, lt
  Multiplexer #(.width(8), .enable("false")) multiplexer_6 (
    .in0(Line2Mem[15:8]), .in1(multiplexer_1_out), .out(multiplexer_6_out), .sel(comparator_2_eq));
  Comparator #(.width(2), .mode("unsigned")) comparator_3 (
    .a(Offset), .b(2'b10), .eq(comparator_3_eq));  // open: gt, lt
  Multiplexer #(.width(8), .enable("false")) multiplexer_7 (
    .in0(Line2Mem[23:16]), .in1(multiplexer_1_out), .out(multiplexer_7_out), .sel(comparator_3_eq));
  Comparator #(.width(2), .mode("unsigned")) comparator_4 (
    .a(Offset), .b(2'b11), .eq(comparator_4_eq));  // open: gt, lt
  Multiplexer #(.width(8), .enable("false")) multiplexer_8 (
    .in0(Line2Mem[31:24]), .in1(multiplexer_1_out), .out(multiplexer_8_out), .sel(comparator_4_eq));
  Multiplexer #(.width(8), .enable("false")) multiplexer_9 (
    .in0(ReadValue), .in1(WriteVal), .out(multiplexer_9_out), .sel(Write));
  // Probe on Age_2
  Comparator #(.width(2), .mode("unsigned")) comparator_5 (
    .a(Offset), .b(2'b00), .eq(comparator_5_eq));  // open: gt, lt
  Multiplexer #(.width(8), .enable("false")) multiplexer_10 (
    .in0(LineFromMem[7:0]), .in1(multiplexer_9_out), .out(multiplexer_10_out), .sel(comparator_5_eq));
  Comparator #(.width(2), .mode("unsigned")) comparator_6 (
    .a(Offset), .b(2'b01), .eq(comparator_6_eq));  // open: gt, lt
  Multiplexer #(.width(8), .enable("false")) multiplexer_11 (
    .in0(LineFromMem[15:8]), .in1(multiplexer_9_out), .out(multiplexer_11_out), .sel(comparator_6_eq));
  Comparator #(.width(2), .mode("unsigned")) comparator_7 (
    .a(Offset), .b(2'b10), .eq(comparator_7_eq));  // open: gt, lt
  Multiplexer #(.width(8), .enable("false")) multiplexer_12 (
    .in0(LineFromMem[23:16]), .in1(multiplexer_9_out), .out(multiplexer_12_out), .sel(comparator_7_eq));
  Comparator #(.width(2), .mode("unsigned")) comparator_8 (
    .a(Offset), .b(2'b11), .eq(comparator_8_eq));  // open: gt, lt
  Multiplexer #(.width(8), .enable("false")) multiplexer_13 (
    .in0(LineFromMem[31:24]), .in1(multiplexer_9_out), .out(multiplexer_13_out), .sel(comparator_8_eq));
  Multiplexer #(.enable("false")) multiplexer_14 (.in0(Dirty), .in1(1'b1), .out(multiplexer_14_out), .sel(Write));
  Multiplexer #(.enable("false")) multiplexer_15 (.in0(Valid), .in1(1'b1), .out(multiplexer_15_out), .sel(Evict));
  Comparator #(.width(7), .mode("unsigned")) comparator_9 (.a(Tag2Mem), .b(Tag), .eq(comparator_9_eq));  // open: gt, lt
  Register #(.width(1)) u_Dirty (.D(multiplexer_14_out), .Q(Dirty), .clk(CLK), .clr(or_2_out));  // open: en
  or or_2 (or_2_out, init, Evict);
  Register #(.width(1)) u_Valid (.D(multiplexer_15_out), .Q(Valid), .clk(CLK), .clr(init));  // open: en
  and and_1 (Contained, comparator_9_eq, Valid);
  Multiplexer #(.width(32), .enable("false")) multiplexer_16 (
    .in0({multiplexer_8_out, multiplexer_7_out, multiplexer_6_out, multiplexer_5_out}),
    .in1(multiplexer_17_out), .out(multiplexer_16_out), .sel(Evict));
  Multiplexer #(.width(32), .enable("false")) multiplexer_17 (
    .in0(Line2Mem), .in1({multiplexer_13_out, multiplexer_12_out, multiplexer_11_out, multiplexer_10_out}),
    .out(multiplexer_17_out), .sel(Write));
  Register #(.width(32)) FullLine (.D(multiplexer_16_out), .Q(Line2Mem), .clk(CLK));  // open: en, clr
  // Probe on Line2Mem

  // Other names for the same wires on the sheet: CurAge[1:0] = Age_2; CurLine[31:0] = Line2Mem;
  //   CurLine07[7:0] = Line2Mem[7:0]; CurLine815[7:0] = Line2Mem[15:8]; CurLine1623[7:0] = Line2Mem[23:16];
  //   CurLine2431[7:0] = Line2Mem[31:24]; CurTag[6:0] = Tag2Mem; InputAge[1:0] = Age; InputTag[6:0] = Tag;
  //   LineFromMem07[7:0] = LineFromMem[7:0]; LineFromMem815[7:0] = LineFromMem[15:8];
  //   LineFromMem1623[7:0] = LineFromMem[23:16]; LineFromMem2431[7:0] = LineFromMem[31:24]
endmodule

module FSM (
  input  State2,
  input  State1,
  input  State0,
  input  Write,
  input  Dirty,
  input  Contains,
  input  Start,
  output NextState2,
  output NextState1,
  output NextState0
);

  wire and_1_out, and_2_out, and_3_out, and_4_out, and_5_out, and_6_out, and_7_out, and_8_out, and_9_out,
       and_10_out, and_11_out, and_12_out, not_1_out, not_2_out, not_3_out, not_4_out, not_5_out, not_6_out,
       not_7_out, not_8_out, not_9_out, not_10_out, not_11_out, not_12_out, not_13_out, not_14_out,
       not_15_out, not_16_out;

  not not_1 (not_1_out, State0);
  not not_2 (not_2_out, Contains);
  not not_3 (not_3_out, State2);
  not not_4 (not_4_out, State1);
  not not_5 (not_5_out, State2);
  not not_6 (not_6_out, State1);
  not not_7 (not_7_out, State0);
  not not_8 (not_8_out, State2);
  not not_9 (not_9_out, State0);
  not not_10 (not_10_out, State2);
  not not_11 (not_11_out, State1);
  not not_12 (not_12_out, Start);
  not not_13 (not_13_out, State1);
  not not_14 (not_14_out, State0);
  not not_15 (not_15_out, State0);
  not not_16 (not_16_out, State0);
  and and_1 (and_1_out, State1, not_1_out, not_2_out);
  and and_2 (and_2_out, not_3_out, State1, State0, Write);
  and and_3 (and_3_out, State2, not_4_out, State0);
  and and_4 (and_4_out, not_5_out, not_6_out, State0, Start);
  and and_5 (and_5_out, State1, not_7_out, Contains);
  and and_6 (and_6_out, not_8_out, State1, State0, Write);
  and and_7 (and_7_out, State2, not_9_out);
  and and_8 (and_8_out, not_10_out, not_11_out, not_12_out);
  and and_9 (and_9_out, not_13_out, not_14_out);
  and and_10 (and_10_out, not_15_out, Contains);
  and and_11 (and_11_out, not_16_out, Dirty);
  and and_12 (and_12_out, State1, State0);
  or or_1 (NextState2, and_1_out, and_2_out, and_3_out);
  or or_2 (NextState1, and_4_out, and_5_out, and_6_out, and_7_out);
  or or_3 (NextState0, and_8_out, and_9_out, and_10_out, and_11_out, and_12_out);
endmodule
